# Fritzing sketch alarmclock_mk1 (saved by Fritzing 0.9.3b)
circuit board: 10cm x 5cm
breadboards: 2

parts:
  The_nano = Arduino Nano (Rev3.0)
  Select_Encoder = Rotary Encoder [package=THT]
  Select_Button = Pushbutton [package="[THT]"]
  J1 = Camdenboss CTB0158-4 [part_number=CTB0158-4 package=THT]
  SPKR1 = Loudspeaker
  Led_8x8_Display = LED Matrix - Serial Interface - Red/Green/Blue
  Radio = Digital FM Radio Receiver
  Snooze_Button = Pushbutton [package="[THT]"]
  Master_Switch = Pushbutton [package=THT]
  Amplifier = LM386 [package=dip08]
  C1 = Electrolytic Capacitor [capacitance=100µF voltage=10V package="100 mil [THT, electrolytic]"]
  C2 = Ceramic Capacitor [capacitance=100nF voltage=10V package="100 mil [THT, multilayer]"]
  C3 = Electrolytic Capacitor [capacitance=100µF package="100 mil [THT, electrolytic]"]
  P1_Volume = Rotary Potentiometer (Small) [maximum_resistance=20k package=THT]
  Phones_Out = rounded female pin header, 1 pin [form="♀ (female rounded)"]
  Led_Power = rounded female pin header, 2 pins [form="♀ (female rounded)"]
  Led_Data = rounded female pin header, 3 pins [form="♀ (female rounded)"]  # not connected
  Switches_Bus = rounded female pin header, 6 pins [form="♀ (female rounded)"]
  9_V = Power plug
  R1 = Resistor [tolerance=±5% resistance=100k package=THT]

nets (from the schematic view):
  GND: The_nano.GND, Select_Encoder.EncoderPinC, Select_Button.Pin_3, Select_Button.Pin_4, J1.pin2, J1.pin3, SPKR1.pin1, Led_8x8_Display.GND, Radio.GND, Snooze_Button.Pin_1, Snooze_Button.Pin_2, Master_Switch.leg0, Amplifier.+IN, Amplifier.V-, C3.-, Led_Power.pin1, Switches_Bus.pin6, 9_V.GND
  N1: The_nano.D2, Radio.!RST
  N2: The_nano.D5, Master_Switch.leg1
  N3: The_nano.D6, Select_Encoder.EncoderPinB
  N4: The_nano.D7, Select_Encoder.EncoderPinA
  N5: The_nano.D8, Select_Button.Pin_1, Select_Button.Pin_2
  N6: The_nano.D9, Snooze_Button.Pin_3, Snooze_Button.Pin_4
  N7: The_nano.D10, Led_8x8_Display.SCK
  N8: The_nano.D11/MOSI, Led_8x8_Display.CS
  N9: The_nano.D12/MISO, Led_8x8_Display.MOSI
  VIN: The_nano.VIN, J1.pin4, Amplifier.V+, C3.+, 9_V.VCC
  N10: The_nano.A5, Radio.SCLK
  N11: The_nano.A4, Radio.SDIO
  3V3: The_nano.3V3, Radio.3.3V
  N12: J1.pin1, SPKR1.pin2, C1.-
  N13: Led_8x8_Display.VCC, Led_Power.pin2
  N14: Amplifier.-IN, C2.1
  N15: Amplifier.OUT, C1.+
  N16: C2.0, P1_Volume.wiper
  N17: P1_Volume.leg2, R1.Pin_1
  N18: Phones_Out.pin1, R1.Pin_0
